# Fritzing sketch datn (saved by Fritzing 0.9.3b)

parts:
  U1 = NodeMCU V1.0
  Part1 = RFID-RC522-v3
  Part2 = OLED Monochrome 128x32 I2C [part_number=931]

nets:
  N1: U1.D1, Part2.SDA
  N2: U1.D2, Part2.SCL
  N3: U1.D3, Part1.RST
  N4: U1.D4, Part1.SDA
  3V3: U1.3V3, Part1.3.3V
  GND: U1.GND, Part2.GND
  N5: U1.D5, Part1.SCK
  N6: U1.D6, Part1.MISO
  N7: U1.D7, Part1.MOSI
  VIN: U1.Vin, Part2.VIN

custom parts:
  NodeMCU V1.0: ESP8266 based NodeMCU
  RFID-RC522-v3: A simple China made RFID-RC522 Reader (6x4 cm); do check the pin labels, as this is a MFRC522 based clone.
  OLED Monochrome 128x32 I2C: These displays are small, only about 1" diagonal, but very readable due to the high contrast of an OLED display. This display is made of 128x32 individual white OLED pixels, each one is turned on or off by the controller chip. Because the display makes its own light, no backlight is required. This reduces the power required to run the OLED and is why the display has such high contrast; we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
